# Fritzing sketch Fritizing_motor+esp+arduino (saved by Fritzing 1.0.2b)
breadboards: 1

parts:
  Componente1 = Arduino Uno (Rev3) - ICSP
  Mod1 = Amica NodeMCU DEVKIT 1.0
  L298N1 = L298N DC motor driver
  M1 = DC Motor [voltage_(max)=6V voltage_(min)=3V]
  M2 = DC Motor [voltage_(max)=6V voltage_(min)=3V]
  M3 = RioRand LM2596
  VCC1 = Battery block 9V

nets:
  N1: Componente1.D9_PWM, L298N1.ENA
  N2: Componente1.D10_PWM/SS, L298N1.ENB
  N3: Componente1.D2, Mod1.pin3
  N4: Componente1.D3_PWM, Mod1.pin4
  N5: Componente1.3V3, L298N1.IN1, L298N1.IN4
  GND: Componente1.GND, L298N1.GND, L298N1.IN2, L298N1.IN3, VCC1.-
  N6: Mod1.pin_29, M3.Pin_4
  N7: Mod1.pin_30, M3.Pin_3
  N8: L298N1.OUT1, M1.pin_2
  N9: L298N1.OUT2, M1.pin_1
  N10: L298N1.OUT3, M2.pin_1
  N11: L298N1.OUT4, M2.pin_2
  N12: L298N1.12V, M3.Pin_1, VCC1.+

notes:
  12V

custom parts:
  L298N DC motor driver: 2x DC motor driver with 78M05 positive voltage regulator (7..35 V) L298N: max 46 V, 2 A Set 5 V Enable jumper to enable 5 V regultor (needed for the L298N) and +5 V output at screw terminal or supply external +5 V at screw terminal Set ENA and/or ENB to +5 V to enable motor permanently or supply ENA and/or ENB with PWM signal IN1 and IN2 set rotation directory for motor A (OUT1/OUT2) IN2 and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
