# Fritzing sketch joystick (saved by Fritzing 1.0.2b)
breadboards: 1

parts:
  R1 = Rotary Potentiometer (Small) [maximum_resistance=10kΩ knob_status=50% power=0.5W package=THT]
  R2 = Rotary Potentiometer (Small) [maximum_resistance=10kΩ knob_status=50% power=0.5W package=THT]
  Mod1 = Amica NodeMCU DEVKIT 1.0
  Componente1 = Arduino Mega 2560 (Rev3)
  S1 = Pushbutton [package="[THT]"]
  S2 = Pushbutton [package="[THT]"]

nets:
  N1: R1.leg1, R2.leg1, Componente1.5V
  N2: R1.wiper, Componente1.A15
  N3: R1.leg2, R2.leg2, Mod1.pin2, Mod1.pin_25, Componente1.GND, S1.Pin_3, S1.Pin_4, S2.Pin_3, S2.Pin_4
  N4: R2.wiper, Componente1.A13
  N5: Mod1.pin3, Componente1.D17_PWM/RX2
  N6: Mod1.pin4, Componente1.D16_PWM/TX2
  N7: Componente1.A9, S1.Pin_1, S1.Pin_2
  N8: Componente1.A10, S2.Pin_1, S2.Pin_2
